# Fritzing sketch rc522-wemos (saved by Fritzing 0.9.9b)
circuit board: 5.64444cm x 8.46667cm
breadboards: 1

parts:
  RC5222 = RFID-RC522 [part_number=101218]
  WeMos_D1_Mini1 = WeMos D1 Mini

nets:
  N1: RC5222.SDA, WeMos_D1_Mini1.D8
  N2: RC5222.SCK, WeMos_D1_Mini1.D5
  N3: RC5222.MOSI, WeMos_D1_Mini1.D7
  N4: RC5222.MISO, WeMos_D1_Mini1.D6
  N5: RC5222.GND, WeMos_D1_Mini1.G
  3.3V: RC5222.3.3V, WeMos_D1_Mini1.3V3
